# Fritzing sketch DIGITAL_LED (saved by Fritzing 0.9.0b)
breadboards: 1

parts:
  Part1 = Arduino Uno (Rev3)
  S1 = Pushbutton [package="[THT]"]
  S2 = Pushbutton [package="[THT]"]
  R1 = Resistor [tolerance=±5% resistance=10k package=THT]
  R2 = Resistor [tolerance=±5% resistance=10k package=THT]
  U1 = 7-SEGMENT-DISPLAY [package=7-segment-display]
  U2 = 7-SEGMENT-DISPLAY [package=7-segment-display]  # not connected

nets:
  N1: Part1.D11_PWM/MOSI, U1.C
  N2: Part1.D12/MISO, U1.DP
  N3: Part1.D13/SCK, U1.B
  N4: Part1.D5_PWM, S2.Pin_1, S2.Pin_2, R2.Pin_0
  N5: Part1.D6_PWM, S1.Pin_1, S1.Pin_2, R1.Pin_0
  N6: Part1.5V, S1.Pin_3, S1.Pin_4, S2.Pin_3, S2.Pin_4, U1.D
  N7: Part1.GND, R1.Pin_1, R2.Pin_1, U1.G1
