# Fritzing sketch CONTROLLER (saved by Fritzing 0.9.3b)
breadboards: 1

parts:
  U1 = atmega328 [package=dip]
  VCC1 = Battery block 9V
  U2 = Voltage Regulator - 5V [package="DPak [SMD]"]
  U3 = V_REG_LD1117VXX [package=78xxl]
  C1 = Electrolytic Capacitor [capacitance=10μF voltage=10V package="0605 [SMD, electrolytic]"]
  C2 = Electrolytic Capacitor [capacitance=10μF voltage=10V package="0605 [SMD, electrolytic]"]
  C3 = Electrolytic Capacitor [capacitance=10μF voltage=10V package="0605 [SMD, electrolytic]"]
  C4 = Capacitor [package=cap-pth-small2]
  XTAL1 = Crystal [frequency="16 Mhz" package=THT]
  C5 = Capacitor [package=cap-pth-small2]

nets:
  N1: U1.VCC, U1.AVCC
  N2: U1.XLAT1, C4.1, XTAL1.pin_0
  N3: U1.XLAT2, XTAL1.pin_1, C5.1
  GND: VCC1.-, U2.input_voltage, U2.GND, U3.GND, C1.-, C1.+, C2.-, C3.-
  N4: VCC1.+, C4.2, C5.2
  N5: U2.output_voltage, U3.IN, C2.+
  N6: U3.OUT, C3.+
